# Fritzing sketch Fridge 1 (saved by Fritzing 1.0.4)
breadboards: 2

parts:
  M1 = RioRand LM2596
  Mod1 = Amica NodeMCU DEVKIT 1.0
  RE1 = KY-040 Rotary encoder [package=THT]
  A1 = 2 channel relay module [package=THT]
  Part1 = Adafruit PCF8574 [part_number="Adafruit #5545"]
  Part2 = OLED Monochrome 128x64 1.3 inch [part_number=938]
  DS1 = DS18B20 1-Wire Temperature Sensor [part_number=DS18B20]
  DS2 = DS18B20 1-Wire Temperature Sensor [part_number=DS18B20]
  U2 = Voltage Regulator - 3.3V [package="TO220 [THT]"]
  R1 = Resistor [tolerance=±5% power=0.25W resistance=4.7k package=THT]
  R2 = Resistor [tolerance=±5% power=0.25W resistance=10k package=THT]
  R3 = Resistor [tolerance=±5% power=0.25W resistance=10k package=THT]
  R4 = Resistor [tolerance=±5% power=0.25W resistance=2.2k package=THT]
  R5 = Resistor [tolerance=±5% power=0.25W resistance=10k package=THT]
  R6 = Resistor [tolerance=±5% power=0.25W resistance=1.5k package=THT]

nets:
  N1: M1.Pin_1, A1.Pin_11
  N2: M1.Pin_3, Mod1.pin_30, A1.Pin_25
  GND: M1.Pin_4, Mod1.pin2, Mod1.pin_9, Mod1.pin_25, Mod1.pin_29, RE1.GND, A1.Pin_26, Part1.GND, Part2.GND, R4.Pin_0
  VCC: Mod1.pin1, Mod1.pin_10, Mod1.pin_26, RE1.Vcc, Part1.VCC, Part2.VIN, R2.Pin_1, R3.Pin_1
  N3: Mod1.pin4, DS1.DQ, DS2.DQ, R1.Pin_1
  N4: Mod1.pin7, RE1.CLK, R3.Pin_0
  N5: Mod1.pin8, RE1.DT, R2.Pin_0
  N6: Mod1.pin_11, RE1.SW
  N7: Mod1.pin_13, Part1.SDA, Part2.MOSI_SDA
  N8: Mod1.pin_14, Part1.SCL, Part2.SCLK_SCK
  N9: A1.Pin_1, R6.Pin_0
  N10: A1.Pin_15, Part1.P0
  N11: A1.Pin_18, Part1.P1
  N12: A1.Pin_21, Part1.P2
  N13: A1.Pin_24, Part1.P3
  N14: Part1.P4, R4.Pin_1, R5.Pin_1
  GND_2: DS1.GND, DS2.GND, U2.GND
  VDD: DS1.VDD, DS2.VDD, U2.output_voltage, R1.Pin_0

notes:
  BD35 Thermostat
  Internal Fan Power
  External Fan Power
  Power to BD35
  12V input from fridge power switch
  12V power to fridge controller
  5V outout from buck convertor
  Rotary control switch
  12V supply to internal fridge thermometers
  DS18B20 with 3V3 psu
  Controller Display
  ESP8266 controller
  3V3 supply from ESP8266
  Speed Control Resistor see BD35 docs

custom parts:
  KY-040 Rotary encoder: KY-040 Rotary Encoder with switch on breakout borad from AZ Delivery
  2 channel relay module: 4 channel Relay Module 5V 12V 24V High and Low Level Trigger Relay Control With Optocoupler Two Way relays DC 5 V 12 V 24 V Volt.
  Adafruit PCF8574: Expand your project possibilities, with the Adafruit PCF8574 GPIO Expander Breakout - an affordable 8 channel I2C expander. GPIO expanders work like this: you have a board with some number of GPIO but not enough for your project - maybe you need more buttons or LEDs. You could upgrade to a board with massive number of GPIO like the Grand Central, or you could pop on one of these boards.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
  OLED Monochrome 128x64 1.3 inch: These displays are small, only about 1.3" diagonal, but very readable due to the high contrast of an OLED display. This display is made of 128x64 individual white OLED pixels, each one is turned on or off by the controller chip. Because the display makes its own light, no backlight is required. This reduces the power required to run the OLED and is why the display has such high contrast; we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
